# Fritzing sketch spidey sense (saved by Fritzing 1.0.4)
breadboards: 1

parts:
  A1 = Particle - Photon2
  OLED_I2C1 = OLED 128x64 I2C Monochrome Display
  OLED_I2C2 = OLED 128x64 I2C Monochrome Display
  M1 = BMP280
  S1 = Pushbutton [package="[THT]"]
  S2 = Pushbutton [package="[THT]"]

nets:
  VDD: A1.Pin_2, A1.Pin_31, OLED_I2C1.VDD, OLED_I2C2.VDD, M1.VIN
  GND: A1.Pin_4, A1.Pin_32, OLED_I2C1.GND, OLED_I2C2.GND, M1.GND, S1.Pin_1, S1.Pin_2, S2.Pin_1, S2.Pin_2
  N1: A1.Pin_17, OLED_I2C1.SDA, OLED_I2C2.SDA, M1.SDA
  N2: A1.Pin_18, OLED_I2C1.SCK, OLED_I2C2.SCK, M1.SCL
  N3: A1.Pin_23, S1.Pin_3, S1.Pin_4
  N4: A1.Pin_24, S2.Pin_3, S2.Pin_4

custom parts:
  Particle - Photon2: The Photon 2 is a microcontroller and Wi-Fi networking developed by particle. Features: 802.11a/b/g/n Wi-Fi, 2.4 GHz and 5 GHz Integrated PCB antenna Integrated U.FL connector for external antenna Integrated RF switch BLE 5 using same antenna as Wi-Fi Realtek RTL8721DM MCU ARM Cortex M33 CPU, 200 MHz 2048 KB (2 MB) user application maximum size 3072 KB (3 MB) of RAM available to user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
  BMP280: Temperature Humidity Barometric presure Sensor, I2C
